# Fritzing sketch bzztmachen (saved by Fritzing 1.0.5)
breadboards: 1

parts:
  A1 = Esp32-c3 super mini
  LED2 = LED - 5mm [color="Green (570nm)" current=0.030A package="5 mm [THT]"]
  LED3 = LED - 5mm [color="Blue (430nm)" current=0.030A package="5 mm [THT]"]
  R1 = Resistor [tolerance=±5% resistance=220 package="0805 [SMD]"]
  R2 = Resistor [tolerance=±5% resistance=220 package="0805 [SMD]"]
  LED1 = LED - 5mm [color="Red (633nm)" current=0.030A package="5 mm [THT]"]
  R3 = Resistor [tolerance=±5% resistance=220 package="0805 [SMD]"]
  U1 = Optocoupler [package=THT]
  U2 = Optocoupler [package=THT]
  U3 = Optocoupler [package=THT]
  R4 = Resistor [tolerance=±5% resistance=220 package="0805 [SMD]"]
  R5 = Resistor [tolerance=±5% resistance=220 package="0805 [SMD]"]
  R6 = Resistor [tolerance=±5% resistance=220 package="0805 [SMD]"]
  U4 = Transformer [input_inductance=1H output_inductance=30H input_resistance=1Ω output_resistance=50Ω package=transformer]
  U5 = Transformer [input_inductance=40H output_inductance=10H input_resistance=1Ω output_resistance=1Ω package=transformer]
  U6 = Transformer [input_inductance=40H output_inductance=10H input_resistance=1Ω output_resistance=1Ω package=transformer]
  Q1 = Basic FET N-Channel [package="TO220 [THT]"]
  Q2 = Basic FET N-Channel [package="TO220 [THT]"]
  Q3 = Basic FET N-Channel [package="TO220 [THT]"]
  R7 = Resistor [tolerance=±5% resistance=2.2k power=0.25W package="0805 [SMD]"]
  R8 = Resistor [tolerance=±5% resistance=2.2k power=0.25W package="0805 [SMD]"]
  R9 = Resistor [tolerance=±5% resistance=2.2k power=0.25W package="0805 [SMD]"]
  R10 = Resistor [tolerance=±5% resistance=1k package="0805 [SMD]"]
  R11 = Resistor [tolerance=±5% resistance=1k package="0805 [SMD]"]
  R12 = Resistor [tolerance=±5% resistance=1k package="0805 [SMD]"]
  VCC1 = Battery block 9V [internal_resistance=0.1Ω]
  V1 = DC Power [voltage=5V internal_resistance=0.1Ω]

nets:
  N1: A1.Pin_7, LED2.anode
  N2: A1.Pin_8, LED3.anode
  N3: A1.Pin_9, U3.Pin_1
  N4: A1.Pin_10, U1.Pin_1
  N5: A1.Pin_11, U2.Pin_1
  N6: A1.Pin_12, LED1.anode
  N7: A1.Pin_15, R1.Pin_1, R2.Pin_1, R3.Pin_1, R4.Pin_1, R5.Pin_1, R6.Pin_1, V1.V-
  N8: A1.Pin_16, V1.V+
  N9: LED2.cathode, R2.Pin_0
  N10: LED3.cathode, R1.Pin_0
  N11: LED1.cathode, R3.Pin_0
  N12: U1.Pin_2, R5.Pin_0
  N13: U1.Pin_4, Q2.gate, R8.Pin_0
  N14: U1.Pin_5, U2.Pin_5, U3.Pin_5, U4.1, U5.1, U6.1, VCC1.+
  N15: U2.Pin_2, R6.Pin_0
  N16: U2.Pin_4, Q3.gate, R9.Pin_0
  N17: U3.Pin_2, R4.Pin_0
  N18: U3.Pin_4, Q1.gate, R7.Pin_0
  N19: U4.2, Q1.drain
  N20: U4.3, R10.Pin_0
  N21: U5.2, Q2.drain
  N22: U5.3, R11.Pin_0
  N23: U6.2, Q3.drain
  N24: U6.3, R12.Pin_0
  N25: Q1.source, Q2.source, Q3.source, R7.Pin_1, R8.Pin_1, R9.Pin_1, VCC1.-

custom parts:
  Esp32-c3 super mini: ESP32-C3 Development Board ESP32 SuperMini Development Board ESP32 Development Board WiFi Bluetooth.
